# Fritzing sketch encoderP (saved by Fritzing 0.9.10b)

parts:
  M1 = RioRand LM2596
  Part1 = Arduino Nano (Rev3.0)
  Driver1 = 28BYJ-48 Driver Module [part_number=ULN2003 package=THT]
  X3 = DB9 Connector [package=db9]
  X4 = DB9 Connector [package=db9]

nets:
  N1: M1.Pin_1, X3.8
  N2: M1.Pin_2, X3.7
  N3: M1.Pin_3, Part1.VIN
  GND: M1.Pin_4, Part1.GND, Driver1.GND, X4.7
  N4: Part1.D2, X4.4
  N5: Part1.D4, X4.3
  N6: Part1.D5, Driver1.IN1
  N7: Part1.5V, X4.8
  N8: Driver1.blue-pin, X3.4

notes:
  BLINK

custom parts:
  28BYJ-48 Driver Module: ULN2003 Driver Module for the 28BYJ-48 Unipolar Stepper Motor LED A - Blue wire - Bottom coil left LED B - Pink wire - Top coil left LED C - Yellow wire - Bottom coil right LED D - Orange wire - Top coil right Common rail - red Connector pins: blue - pink - yellow - orange - red Control pins - IN1 to IN4 Power pins - GND & Vmotor (5-12V) On/Off jumper (if removed, power to motor is cut).

// code stored in the sketch: Blink.ino
/*
DB9 MACHO al controlador
1. nc
2. nc
3. nc
4. Pulsos sintetizados
5. nc
7. GND
8. 24Vcc
9. nc

DB9 HEMBRA al ENCODER
1. nc
2. nc
3. Canal B
4. Canal A
5. GND
6. Canal Z (nc)
7. nc
8. nc
9. 12V

Ajustar la salida del regulador de voltaje a 12V
*/
#include <Arduino.h>


#define canalA  2
#define canalB  4
#define salidaFW 5


int cantidadPulsosEnReversa = 0;


void procesaPulso();


void setup() {
  pinMode (canalA, INPUT_PULLUP);
  pinMode (canalB, INPUT_PULLUP);
  pinMode (salidaFW, OUTPUT);
  digitalWrite(salidaFW, LOW); //pone salida en bajo.
//Interrupción externa 0, D2, dispara por flanco ascendente.  
  attachInterrupt(digitalPinToInterrupt(canalA), procesaPulso, RISING);


}



void loop() {
  //do nothing.
}


void procesaPulso(){


  if( digitalRead(canalB) == LOW ){ 
    if( cantidadPulsosEnReversa ){
       cantidadPulsosEnReversa--;
    } 
    
    else{
      digitalWrite(salidaFW, HIGH);
      while( digitalRead(canalA) == HIGH );
      digitalWrite(salidaFW, LOW);
    }
  }
  else{
    cantidadPulsosEnReversa++;
  }


}
